# Fritzing sketch washer_switch-magnetic-door_and_rgb_led (saved by Fritzing 0.9.10b)
breadboards: 1

parts:
  R6 = Resistor [tolerance=±5% resistance=330 power=0.25 package=THT]
  R7 = Resistor [tolerance=±5% resistance=330 power=0.25 package=THT]
  R10 = Resistor [tolerance=±5% resistance=330 power=0.25 package=THT]
  LED3 = RGB LED (com. cathode, rgb) [package="5 mm [THT]"]
  R11 = Resistor [tolerance=±5% resistance=10k power=0.25 package=THT]
  S4 = Magnetic Door Switch [package=reed_switch_plastic]
  R12 = TRIMPOT [maximum_resistance=10kΩ knob_status=50% power=0.5W package=3362u-2]
  A1 = Particle Photon 2

nets:
  N1: R6.Pin_0, LED3.red_anode
  N2: R6.Pin_1, A1.Pin_7
  N3: R7.Pin_0, LED3.green_anode
  N4: R7.Pin_1, A1.Pin_8
  N5: R10.Pin_0, LED3.blue_anode
  N6: R10.Pin_1, A1.Pin_12
  N7: LED3.common_cathode, S4.2, R12.CW, A1.Pin_4, A1.Pin_30
  N8: R11.Pin_0, R12.CCW, A1.Pin_2
  N9: R11.Pin_1, S4.1, A1.Pin_22
  N10: R12.WIPER, A1.Pin_6
  N11: A1.Pin_28, A1.Pin_29

custom parts:
  Particle Photon 2: The Photon 2 is a development module with a microcontroller and Wi-Fi networking. -- This Fritzing file originally created by Peter Van Epp https://forum.fritzing.org/t/request-particle-photon2/19824/2 5/18/2024 - Rob Parke Rotated breadboard image
