# Fritzing sketch ble_uart_control_fan (saved by Fritzing 0.9.4)
breadboards: 2

parts:
  LED1 = RGB LED (com. cathode, rbg) [package="5 mm [THT]"]
  Part2 = Motor Driver 1A Dual TB6612FNG  # not connected
  J3 = Basic Servo
  Argon2 = Particle Argon
  M2 = DC Motor  # not connected
  R1 = Resistor [tolerance=±5% resistance=330 package="2010 [SMD]"]
  R2 = Resistor [tolerance=±5% resistance=330 package="2010 [SMD]"]
  R3 = Resistor [tolerance=±5% resistance=330 package="2010 [SMD]"]
  J4 = Piezo Speaker

nets:
  N1: LED1.red_anode, R1.Pin_1
  GND: LED1.common_cathode, J3.gnd, Argon2.GND, J4.pin1
  N2: LED1.blue_anode, R2.Pin_1
  N3: LED1.green_anode, R3.Pin_1
  VCC: J3.vcc, Argon2.3.3V
  N4: J3.pulse, Argon2.D2
  N5: Argon2.A0, R1.Pin_0
  N6: Argon2.A2, R2.Pin_0
  N7: Argon2.A3, R3.Pin_0
  N8: Argon2.D6, J4.pin2

custom parts:
  Particle Argon: The Argon is a powerful Wi-Fi enabled development board that can act as either a standalone Wi-Fi endpoint or Wi-Fi enabled gateway for Particle Mesh networks. It is based on the Nordic nRF52840 and has built-in battery charging circuitry so it’s easy to connect a Li-Po and deploy your local network in minutes. The Argon is great for connecting existing projects to the Particle Device Cloud or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
