# Fritzing sketch servo (saved by Fritzing 0.9.10b)
breadboards: 1

parts:
  J1 = Basic Servo
  A1 = Particle Photon 2

nets:
  N1: J1.gnd, A1.Pin_4, A1.Pin_30
  N2: J1.vcc, A1.Pin_2, A1.Pin_31
  N3: J1.pulse, A1.Pin_19
  N4: A1.Pin_28, A1.Pin_29

custom parts:
  Particle Photon 2: The Photon 2 is a development module with a microcontroller and Wi-Fi networking. -- This Fritzing file originally created by Peter Van Epp https://forum.fritzing.org/t/request-particle-photon2/19824/2 5/18/2024 - Rob Parke Rotated breadboard image
