# Fritzing sketch button_latch_one_led (saved by Fritzing 1.0.5)
breadboards: 1

parts:
  S2 = Pushbutton [package="[THT]"]
  R1 = Resistor [tolerance=±5% resistance=10k power=0.25 package=THT]
  LED1 = LED - 5mm [color="Blue (470nm)" current=0.030 package="5 mm [THT]"]
  R3 = Resistor [tolerance=±5% resistance=330 power=0.25 package=THT]
  A1 = Particle Photon 2

nets:
  N1: S2.Pin_1, S2.Pin_2, R3.Pin_0, A1.Pin_4, A1.Pin_30
  N2: S2.Pin_3, S2.Pin_4, R1.Pin_0, A1.Pin_19
  N3: R1.Pin_1, A1.Pin_2, A1.Pin_31
  N4: LED1.cathode, R3.Pin_1
  N5: LED1.anode, A1.Pin_7
  N6: A1.Pin_28, A1.Pin_29

custom parts:
  Particle Photon 2: The Photon 2 is a development module with a microcontroller and Wi-Fi networking. -- This Fritzing file originally created by Peter Van Epp https://forum.fritzing.org/t/request-particle-photon2/19824/2 5/18/2024 - Rob Parke Rotated breadboard image
