# Fritzing sketch switch-magnetic-door (saved by Fritzing 0.9.10b)
breadboards: 1

parts:
  S3 = Magnetic Door Switch [package=reed_switch_plastic]
  R2 = Resistor [tolerance=±5% resistance=10k power=0.25 package=THT]
  A1 = Particle Photon 2

nets:
  N1: S3.1, R2.Pin_1, A1.Pin_19
  N2: S3.2, A1.Pin_4, A1.Pin_30
  N3: R2.Pin_0, A1.Pin_2, A1.Pin_31
  N4: A1.Pin_28, A1.Pin_29

custom parts:
  Particle Photon 2: The Photon 2 is a development module with a microcontroller and Wi-Fi networking. -- This Fritzing file originally created by Peter Van Epp https://forum.fritzing.org/t/request-particle-photon2/19824/2 5/18/2024 - Rob Parke Rotated breadboard image
