# Fritzing sketch speaker (saved by Fritzing 0.9.10b)
breadboards: 1

parts:
  J1 = Piezo Speaker
  A1 = Particle Photon 2

nets:
  N1: J1.pin1, A1.Pin_4, A1.Pin_30, A1.Pin_35
  N2: J1.pin2, A1.Pin_8
  N3: A1.Pin_28, A1.Pin_29

custom parts:
  Particle Photon 2: The Photon 2 is a development module with a microcontroller and Wi-Fi networking. -- This Fritzing file originally created by Peter Van Epp https://forum.fritzing.org/t/request-particle-photon2/19824/2 5/18/2024 - Rob Parke Rotated breadboard image
