# Fritzing sketch speaker_pot (saved by Fritzing 0.9.10b)
breadboards: 1

parts:
  U2 = POT [knob_status=50% power=0.5W package=3362u]
  J2 = Piezo Speaker
  A2 = Particle Photon 2

nets:
  N1: U2.S, A2.Pin_4, A2.Pin_30
  N2: U2.A, J2.pin1
  N3: J2.pin2, A2.Pin_8
  N4: A2.Pin_28, A2.Pin_29

custom parts:
  Particle Photon 2: The Photon 2 is a development module with a microcontroller and Wi-Fi networking. -- This Fritzing file originally created by Peter Van Epp https://forum.fritzing.org/t/request-particle-photon2/19824/2 5/18/2024 - Rob Parke Rotated breadboard image
