# Fritzing sketch ultrasonic (saved by Fritzing 0.9.10b)
breadboards: 1

parts:
  HC-SR04_Sensor_1 = HC-SR04 Ultrasonic Distance Sensor
  A1 = Particle Photon 2

nets:
  N1: HC-SR04_Sensor_1.VCC, A1.Pin_26
  N2: HC-SR04_Sensor_1.TRIG, A1.Pin_23
  N3: HC-SR04_Sensor_1.ECHO, A1.Pin_22
  N4: HC-SR04_Sensor_1.GND, A1.Pin_4, A1.Pin_30
  N5: A1.Pin_28, A1.Pin_29

custom parts:
  Particle Photon 2: The Photon 2 is a development module with a microcontroller and Wi-Fi networking. -- This Fritzing file originally created by Peter Van Epp https://forum.fritzing.org/t/request-particle-photon2/19824/2 5/18/2024 - Rob Parke Rotated breadboard image
