# Fritzing sketch open_pir_sparkfun_sleep_button (saved by Fritzing 0.9.10b)
breadboards: 1

parts:
  Part7 = HC-SR501 Body Sensor Module
  A1 = Particle Photon 2
  S1 = Pushbutton [package="[THT]"]
  R1 = Resistor [tolerance=±5% power=0.25 resistance=220 package=THT]

nets:
  N1: Part7.VCC, A1.Pin_2, A1.Pin_31, R1.Pin_0
  N2: Part7.OUT, S1.Pin_1, S1.Pin_2
  N3: Part7.GND, A1.Pin_19
  N4: A1.Pin_4, A1.Pin_30
  N5: A1.Pin_25, S1.Pin_3, S1.Pin_4, R1.Pin_1
  N6: A1.Pin_28, A1.Pin_29

notes:
  Note: Sparkfun OpenPIR looks different

custom parts:
  HC-SR501 Body Sensor Module: Pyroelectric Infrared PIR Motion Sensor Detector Module
  Particle Photon 2: The Photon 2 is a development module with a microcontroller and Wi-Fi networking. -- This Fritzing file originally created by Peter Van Epp https://forum.fritzing.org/t/request-particle-photon2/19824/2 5/18/2024 - Rob Parke Rotated breadboard image
