# Fritzing sketch pir_sparkfun (saved by Fritzing 1.0.5)
breadboards: 1

parts:
  Part7 = HC-SR501 Body Sensor Module
  R1 = Resistor [tolerance=±5% resistance=10k package="2010 [SMD]"]
  A1 = Particle Photon 2

nets:
  N1: Part7.VCC, R1.Pin_1, A1.Pin_19
  N2: Part7.GND, R1.Pin_0, A1.Pin_26
  N3: A1.Pin_4, A1.Pin_30
  N4: A1.Pin_28, A1.Pin_29

notes:
  Note Sparkfun PIR wiring

custom parts:
  HC-SR501 Body Sensor Module: Pyroelectric Infrared PIR Motion Sensor Detector Module
  Particle Photon 2: The Photon 2 is a development module with a microcontroller and Wi-Fi networking. -- This Fritzing file originally created by Peter Van Epp https://forum.fritzing.org/t/request-particle-photon2/19824/2 5/18/2024 - Rob Parke Rotated breadboard image
